// Digital circuit AY-3-8910.dig as structural Verilog
module AY_3_8910 (
  input  [7:0] DA0__7,
  input  CLOCK,
  input  nRESET,
  input  BDIR,
  input  BC1,
  input  nA9,
  input  A8,
  output AnalogChA,
  output AnalogChB,
  output AnalogChC
);

  wire _7474_1_p2, _7474_1_p6, _7474_1_p11, _7474_1_p13, _7474_2_p12, _7474_3_p6, _7474_3_p11, _7485_1_p6,
       _7485_1_p7, _7485_1_p8, _7485_2_p6, _7485_2_p7, _7485_2_p8, _7485_3_p6, _7485_3_p7, _7485_3_p8,
       _7485_4_p6, _7485_5_p6, _7485_5_p7, _7485_5_p8, _7485_6_p6, _7485_6_p7, _7485_6_p8, _7485_7_p6,
       _7485_8_p6, _7485_8_p7, _7485_8_p8, _7485_9_p6, _7485_9_p7, _7485_9_p8, _7485_10_p6, _7485_11_p6,
       _7485_11_p7, _7485_11_p8, _7485_12_p6, _7485_12_p7, _7485_12_p8, _7485_13_p6, _7485_14_p6,
       _7485_14_p7, _7485_14_p8, _7485_15_p6, _74112_1_p4, _74112_1_p5, _74112_1_p13, _74112_1_p14,
       _74112_2_p13, _74125_1_p11, _74125_1_p12, _74125_1_p13, _74125_1_p14, _74125_2_p11, _74125_2_p12,
       _74125_2_p13, _74125_2_p14, _74125_3_p11, _74125_3_p12, _74125_3_p13, _74125_3_p14, _74125_4_p11,
       _74125_4_p12, _74125_4_p13, _74125_4_p14, _74125_5_p11, _74125_5_p12, _74125_5_p13, _74125_5_p14,
       _74125_6_p11, _74125_6_p12, _74125_6_p13, _74125_6_p14, _74125_7_p11, _74125_7_p12, _74125_7_p13,
       _74125_7_p14, _74125_8_p11, _74125_8_p12, _74125_8_p13, _74125_8_p14, _74125_9_p11, _74125_9_p12,
       _74125_9_p13, _74125_9_p14, _74125_10_p11, _74125_10_p12, _74125_10_p13, _74125_10_p14, _74125_11_p11,
       _74125_11_p12, _74125_11_p13, _74125_11_p14, _74125_12_p11, _74125_12_p12, _74125_12_p13,
       _74125_12_p14, _74138_5_p9, _74138_5_p10, _74138_5_p11, _74138_5_p12, _74138_5_p13, _74138_5_p14,
       _74138_5_p15, _74138_5_p16, _74138_6_p9, _74138_6_p10, _74138_6_p11, _74138_6_p12, _74138_6_p13,
       _74138_6_p14, _74138_6_p15, _74138_6_p16, _74138_7_p9, _74138_7_p10, _74138_7_p11, _74138_7_p12,
       _74138_7_p13, _74138_7_p14, _74138_7_p15, _74138_7_p16, _74138_8_p9, _74138_8_p10, _74138_8_p11,
       _74138_8_p12, _74138_8_p13, _74138_8_p14, _74138_8_p15, _74138_8_p16, _74138_9_p9, _74138_9_p10,
       _74138_9_p11, _74138_9_p12, _74138_9_p13, _74138_9_p14, _74138_9_p15, _74138_9_p16, _74138_10_p9,
       _74138_10_p10, _74138_10_p11, _74138_10_p12, _74138_10_p13, _74138_10_p14, _74138_10_p15,
       _74138_10_p16, _74191_1_p15, _74273_3_p1, _74273_3_p13, _74273_3_p14, _74273_3_p15, _74273_3_p16,
       _74273_11_p13, _74273_11_p14, _74273_11_p15, _74273_11_p16, _74273_11_p17, _74273_11_p18,
       _74273_12_p13, _74273_12_p14, _74273_12_p16, _74273_13_p4, _74273_13_p5, _74273_13_p6, _74273_13_p7,
       _74273_13_p8, _74273_13_p9, _74273_13_p10, _74273_13_p20, _74273_14_p4, _74273_14_p5, _74273_14_p6,
       _74273_14_p7, _74273_14_p8, _74273_14_p9, _74273_14_p10, _74273_14_p19, _74273_15_p4, _74273_16_p13,
       _74273_16_p14, _74273_16_p15, _74273_16_p16, _74273_16_p17, _74273_17_p13, _74273_17_p14,
       _74273_17_p15, _74273_17_p16, _74273_17_p17, _74273_18_p13, _74273_18_p14, _74273_18_p15,
       _74273_18_p16, _74273_18_p17, Alt, and_2_out, and_3_out, and_4_out, and_5_out, and_6_out, and_7_out,
       and_8_out, and_9_out, Attack, CLK_16, CLK_256, Hold, nAlt, nand_1_out, nand_2_out, nand_4_out,
       nand_5_out, nand_6_out, nand_7_out, nand_8_out, nand_9_out, nand_10_out, nand_11_out, nand_12_out,
       nand_13_out, nand_14_out, nand_16_out, nand_17_out, nand_18_out, nAttack, nHold, not_2_out, not_3_out,
       not_4_out, not_6_out, nRdAmplitudeA, nRdAmplitudeB, nRdAmplitudeC, nRdEnable, nRdEnvelope_Coarse,
       nRdEnvelope_Fine, nRdEnvShape, nRdNoise, nRdPortA, nRdPortB, nRdToneA_Coarse, nRdToneA_Fine,
       nRdToneB_Coarse, nRdToneB_Fine, nRdToneC_Coarse, nRdToneC_Fine, nRES, nTrig, nWrAmplitudeA,
       nWrAmplitudeB, nWrAmplitudeC, nWrEnable, nWrEnvelope_Coarse, nWrEnvelope_Fine, nWrEnvShape, nWrNoise,
       nWrPortA, nWrPortB, nWrToneA_Coarse, nWrToneA_Fine, nWrToneB_Coarse, nWrToneB_Fine, nWrToneC_Coarse,
       nWrToneC_Fine, or_1_out, or_2_out, or_3_out, or_4_out, or_7_out, or_8_out, or_9_out, or_10_out,
       or_11_out, or_12_out, or_13_out, RES, reset_1_out, Trig, xor_1_out;
  wire [3:0] _74157_1_p16, _74157_2_p16, _74157_3_p13, _74191_1_p11, _74541_1_p3, _74541_1_p7, _74541_2_p3,
       _74541_2_p7, _74541_3_p3, _74541_3_p7, _74541_4_p3, _74541_5_p3, _74541_5_p7, _74541_6_p3,
       _74541_7_p3, _74541_7_p7, _74541_8_p3, _74541_9_p3, _74541_9_p7, _744040_2_q3, _744040_2_q7,
       _744040_3_q0, _744040_3_q4;

  Reset reset_1 (.out(reset_1_out));
  and and_1 (nRES, reset_1_out, nRESET);
  // _74273 _74273_1: pin names not known; wires that end beside it: nWrEnvelope_Coarse, nRES, DA0__7[0], DA0__7[1], DA0__7[2], DA0__7[3], DA0__7[4], DA0__7[5], DA0__7[6], DA0__7[7], 1'b1, 1'b0
  // _74273 _74273_2: pin names not known; wires that end beside it: nWrEnvelope_Fine, nRES, DA0__7[0], DA0__7[1], DA0__7[2], DA0__7[3], DA0__7[4], DA0__7[5], DA0__7[6], DA0__7[7], 1'b1, 1'b0
  nand nand_1 (nand_1_out, CLK_256, _7485_4_p6);
  nand nand_2 (nand_2_out, nRES, nand_1_out);
  not not_1 (RES, nRES);
  not not_2 (not_2_out, nA9);
  // _744040 _744040_1: pin names not known; wires that end beside it: CLOCK, RES, CLK_16, CLK_256
  and and_2 (and_2_out, not_2_out, A8);
  // _74541 _74541_1: pin names not known; wires that end beside it: nRdEnvelope_Coarse, nRdEnvelope_Coarse, _74541_1_p3[0], _74541_1_p3[1], _74541_1_p3[2], _74541_1_p3[3], _74541_1_p7[0], _74541_1_p7[1], _74541_1_p7[2], _74541_1_p7[3], 1'b1, 1'b0, DA0__7[0], DA0__7[1], DA0__7[2], DA0__7[3], DA0__7[4], DA0__7[5], DA0__7[6], DA0__7[7]
  // _74541 _74541_2: pin names not known; wires that end beside it: nRdEnvelope_Fine, nRdEnvelope_Fine, _74541_2_p3[0], _74541_2_p3[1], _74541_2_p3[2], _74541_2_p3[3], _74541_2_p7[0], _74541_2_p7[1], _74541_2_p7[2], _74541_2_p7[3], 1'b1, 1'b0, DA0__7[0], DA0__7[1], DA0__7[2], DA0__7[3], DA0__7[4], DA0__7[5], DA0__7[6], DA0__7[7]
  not not_3 (not_3_out, BC1);
  not not_4 (not_4_out, BDIR);
  // _74273 _74273_3: pin names not known; wires that end beside it: _74273_3_p1, nRES, DA0__7[0], DA0__7[1], DA0__7[2], DA0__7[3], 1'b0, 1'b0, 1'b0, 1'b0, 1'b1, 1'b0, _74273_3_p13, _74273_3_p14, _74273_3_p15, _74273_3_p16
  nand nand_3 (_74273_3_p1, BDIR, and_2_out, BC1);
  nand nand_4 (nand_4_out, BDIR, and_2_out, not_3_out);
  nand nand_5 (nand_5_out, not_4_out, and_2_out, BC1);
  _744040 _744040_2 (
    .nCP(CLK_256), .MR(nand_2_out), .Q0(_744040_2_q3[0]), .Q1(_744040_2_q3[1]), .Q2(_744040_2_q3[2]),
    .Q3(_744040_2_q3[3]), .Q4(_744040_2_q7[0]), .Q5(_744040_2_q7[1]), .Q6(_744040_2_q7[2]),
    .Q7(_744040_2_q7[3]));  // open: Q8, Q9, Q10, Q11
  _744040 _744040_3 (
    .nCP(_744040_2_q7[3]), .MR(nand_2_out), .Q0(_744040_3_q0[0]), .Q1(_744040_3_q0[1]), .Q2(_744040_3_q0[2]),
    .Q3(_744040_3_q0[3]), .Q4(_744040_3_q4[0]), .Q5(_744040_3_q4[1]), .Q6(_744040_3_q4[2]),
    .Q7(_744040_3_q4[3]));  // open: Q8, Q9, Q10, Q11
  // _74138 _74138_1: pin names not known; wires that end beside it: _74273_3_p13, _74273_3_p15, _74273_3_p14, 1'b1, nand_4_out, _74273_3_p16, 1'b1, 1'b0, nWrToneA_Fine, nWrToneA_Coarse, nWrToneB_Fine, nWrToneB_Coarse, nWrToneC_Fine, nWrToneC_Coarse, nWrNoise, nWrEnable
  // _74138 _74138_2: pin names not known; wires that end beside it: _74273_3_p13, _74273_3_p15, _74273_3_p14, _74273_3_p16, nand_4_out, 1'b0, 1'b1, 1'b0, nWrAmplitudeA, nWrAmplitudeB, nWrAmplitudeC, nWrEnvelope_Fine, nWrEnvelope_Coarse, nWrEnvShape, nWrPortA, nWrPortB
  // _74138 _74138_3: pin names not known; wires that end beside it: _74273_3_p13, _74273_3_p15, _74273_3_p13, 1'b1, nand_5_out, _74273_3_p16, 1'b1, 1'b0, nRdToneA_Fine, nRdToneA_Coarse, nRdToneB_Fine, nRdToneB_Coarse, nRdToneC_Fine, nRdToneC_Coarse, nRdNoise, nRdEnable
  // _74138 _74138_4: pin names not known; wires that end beside it: _74273_3_p13, _74273_3_p15, _74273_3_p14, _74273_3_p16, nand_5_out, 1'b0, 1'b1, 1'b0, nRdAmplitudeA, nRdAmplitudeB, nRdAmplitudeC, nRdEnvelope_Fine, nRdEnvelope_Coarse, nRdEnvShape, nRdPortA, nRdPortB
  // _7485 _7485_1: pin names not known; wires that end beside it: 1'b0, 1'b1, 1'b0, 1'b1, 1'b0, _7485_1_p6, _7485_1_p7, _7485_1_p8
  // _7485 _7485_2: pin names not known; wires that end beside it: _7485_1_p6, _7485_1_p7, _7485_1_p8, 1'b1, 1'b0, _7485_2_p6, _7485_2_p7, _7485_2_p8
  // _7485 _7485_3: pin names not known; wires that end beside it: _7485_2_p6, _7485_2_p7, _7485_2_p8, 1'b1, 1'b0, _7485_3_p6, _7485_3_p7, _7485_3_p8
  // _7485 _7485_4: pin names not known; wires that end beside it: _7485_3_p6, _7485_3_p7, _7485_3_p8, 1'b1, 1'b0, _7485_4_p6
  // _74273 _74273_4: pin names not known; wires that end beside it: nWrToneA_Coarse, nRES, DA0__7[0], DA0__7[1], DA0__7[2], DA0__7[3], DA0__7[4], DA0__7[5], DA0__7[6], DA0__7[7], 1'b1, 1'b0
  // _74273 _74273_5: pin names not known; wires that end beside it: nWrToneA_Fine, nRES, DA0__7[0], DA0__7[1], DA0__7[2], DA0__7[3], 1'b0, 1'b0, 1'b0, 1'b0, 1'b1, 1'b0
  // _74273 _74273_6: pin names not known; wires that end beside it: nWrToneB_Coarse, nRES, DA0__7[0], DA0__7[1], DA0__7[2], DA0__7[3], DA0__7[4], DA0__7[5], DA0__7[6], DA0__7[7], 1'b1, 1'b0
  // _74273 _74273_7: pin names not known; wires that end beside it: nWrToneB_Fine, nRES, DA0__7[0], DA0__7[1], DA0__7[2], DA0__7[3], 1'b0, 1'b0, 1'b0, 1'b0, 1'b1, 1'b0
  // _74273 _74273_8: pin names not known; wires that end beside it: nWrToneC_Coarse, nRES, DA0__7[0], DA0__7[1], DA0__7[2], DA0__7[3], DA0__7[4], DA0__7[5], DA0__7[6], DA0__7[7], 1'b1, 1'b0
  // _74273 _74273_9: pin names not known; wires that end beside it: nWrToneC_Fine, nRES, DA0__7[0], DA0__7[1], DA0__7[2], DA0__7[3], 1'b0, 1'b0, 1'b0, 1'b0, 1'b1, 1'b0
  nand nand_6 (nand_6_out, CLK_16, _7485_7_p6);
  nand nand_7 (nand_7_out, CLK_16, _7485_10_p6);
  nand nand_8 (nand_8_out, CLK_16, _7485_13_p6);
  nand nand_9 (nand_9_out, nRES, nand_6_out);
  nand nand_10 (nand_10_out, nRES, nand_7_out);
  nand nand_11 (nand_11_out, nRES, nand_8_out);
  // _74541 _74541_3: pin names not known; wires that end beside it: nRdToneA_Coarse, nRdToneA_Coarse, _74541_3_p3[0], _74541_3_p3[1], _74541_3_p3[2], _74541_3_p3[3], _74541_3_p7[0], _74541_3_p7[1], _74541_3_p7[2], _74541_3_p7[3], 1'b1, 1'b0, DA0__7[0], DA0__7[1], DA0__7[2], DA0__7[3], DA0__7[4], DA0__7[5], DA0__7[6], DA0__7[7]
  // _74541 _74541_4: pin names not known; wires that end beside it: nRdToneA_Fine, nRdToneA_Fine, _74541_4_p3[0], _74541_4_p3[1], _74541_4_p3[2], _74541_4_p3[3], 1'b0, 1'b0, 1'b0, 1'b0, 1'b1, 1'b0, DA0__7[0], DA0__7[1], DA0__7[2], DA0__7[3], DA0__7[4], DA0__7[5], DA0__7[6], DA0__7[7]
  // _74541 _74541_5: pin names not known; wires that end beside it: nRdToneB_Coarse, nRdToneB_Coarse, _74541_5_p3[0], _74541_5_p3[1], _74541_5_p3[2], _74541_5_p3[3], _74541_5_p7[0], _74541_5_p7[1], _74541_5_p7[2], _74541_5_p7[3], 1'b1, 1'b0, DA0__7[0], DA0__7[1], DA0__7[2], DA0__7[3], DA0__7[4], DA0__7[5], DA0__7[6], DA0__7[7]
  // _74541 _74541_6: pin names not known; wires that end beside it: nRdToneB_Fine, nRdToneB_Fine, _74541_6_p3[0], _74541_6_p3[1], _74541_6_p3[2], _74541_6_p3[3], 1'b0, 1'b0, 1'b0, 1'b0, 1'b1, 1'b0, DA0__7[0], DA0__7[1], DA0__7[2], DA0__7[3], DA0__7[4], DA0__7[5], DA0__7[6], DA0__7[7]
  // _74541 _74541_7: pin names not known; wires that end beside it: nRdToneC_Coarse, nRdToneC_Coarse, _74541_7_p3[0], _74541_7_p3[1], _74541_7_p3[2], _74541_7_p3[3], _74541_7_p7[0], _74541_7_p7[1], _74541_7_p7[2], _74541_7_p7[3], 1'b1, 1'b0, DA0__7[0], DA0__7[1], DA0__7[2], DA0__7[3], DA0__7[4], DA0__7[5], DA0__7[6], DA0__7[7]
  // _74541 _74541_8: pin names not known; wires that end beside it: nRdToneC_Fine, nRdToneC_Fine, _74541_8_p3[0], _74541_8_p3[1], _74541_8_p3[2], _74541_8_p3[3], 1'b0, 1'b0, 1'b0, 1'b0, 1'b1, 1'b0, DA0__7[0], DA0__7[1], DA0__7[2], DA0__7[3], DA0__7[4], DA0__7[5], DA0__7[6], DA0__7[7]
  // _744040 _744040_4: pin names not known; wires that end beside it: CLK_16, nand_9_out
  // _744040 _744040_5: pin names not known; wires that end beside it: CLK_16, nand_10_out
  // _744040 _744040_6: pin names not known; wires that end beside it: CLK_16, nand_11_out
  // _7485 _7485_5: pin names not known; wires that end beside it: 1'b0, 1'b1, 1'b0, 1'b1, 1'b0, _7485_5_p6, _7485_5_p7, _7485_5_p8
  // _7485 _7485_6: pin names not known; wires that end beside it: _7485_5_p6, _7485_5_p7, _7485_5_p8, 1'b1, 1'b0, _7485_6_p6, _7485_6_p7, _7485_6_p8
  // _7485 _7485_7: pin names not known; wires that end beside it: _7485_6_p6, _7485_6_p7, _7485_6_p8, 1'b1, 1'b0, _7485_7_p6
  // _7485 _7485_8: pin names not known; wires that end beside it: 1'b0, 1'b1, 1'b0, 1'b1, 1'b0, _7485_8_p6, _7485_8_p7, _7485_8_p8
  // _7485 _7485_9: pin names not known; wires that end beside it: _7485_8_p6, _7485_8_p7, _7485_8_p8, 1'b1, 1'b0, _7485_9_p6, _7485_9_p7, _7485_9_p8
  // _7485 _7485_10: pin names not known; wires that end beside it: _7485_9_p6, _7485_9_p7, _7485_9_p8, 1'b1, 1'b0, _7485_10_p6
  // _7485 _7485_11: pin names not known; wires that end beside it: 1'b0, 1'b1, 1'b0, 1'b1, 1'b0, _7485_11_p6, _7485_11_p7, _7485_11_p8
  // _7485 _7485_12: pin names not known; wires that end beside it: _7485_11_p6, _7485_11_p7, _7485_11_p8, 1'b1, 1'b0, _7485_12_p6, _7485_12_p7, _7485_12_p8
  // _7485 _7485_13: pin names not known; wires that end beside it: _7485_12_p6, _7485_12_p7, _7485_12_p8, 1'b1, 1'b0, _7485_13_p6
  and and_3 (and_3_out, Alt, 1'b1, nHold);
  or or_1 (or_1_out, Attack, nTrig);
  or or_2 (or_2_out, nTrig, nAttack);
  // _74112 _74112_1: pin names not known; wires that end beside it: 1'b0, 1'b0, 1'b0, _74112_1_p4, _74112_1_p5, nTrig, 1'b0, 1'b0, 1'b0, _74112_1_p4, 1'b1, 1'b0, _74112_1_p13, _74112_1_p14
  // _74273 _74273_10: pin names not known; wires that end beside it: nWrNoise, nRES, DA0__7[0], DA0__7[1], DA0__7[2], DA0__7[3], DA0__7[4], DA0__7[5], DA0__7[6], DA0__7[7], 1'b1, 1'b0
  nand nand_12 (nand_12_out, CLK_16, _7485_15_p6);
  // _74273 _74273_11: pin names not known; wires that end beside it: nWrEnable, nRES, DA0__7[0], DA0__7[1], DA0__7[2], DA0__7[3], DA0__7[4], DA0__7[5], 1'b0, 1'b0, 1'b1, 1'b0, _74273_11_p13, _74273_11_p14, _74273_11_p15, _74273_11_p16, _74273_11_p17, _74273_11_p18
  // _74273 _74273_12: pin names not known; wires that end beside it: nWrEnvShape, nRES, DA0__7[0], DA0__7[1], DA0__7[2], DA0__7[3], 1'b0, 1'b0, 1'b0, 1'b0, 1'b1, 1'b0, _74273_12_p13, _74273_12_p14, Attack, _74273_12_p16
  // _74112 _74112_2: pin names not known; wires that end beside it: _74112_1_p4, and_3_out, and_3_out, or_1_out, or_2_out, 1'b1, 1'b0, 1'b0, 1'b0, 1'b1, 1'b1, 1'b0, _74112_2_p13
  xor xor_1 (xor_1_out, _74273_15_p4, _74273_14_p9);
  // _7474 _7474_1: pin names not known; wires that end beside it: 1'b1, _7474_1_p2, nand_6_out, 1'b1, 1'b1, _7474_1_p6, nand_7_out, 1'b1, 1'b1, 1'b0, _7474_1_p11, _7474_1_p2, _7474_1_p13, _7474_1_p6
  and and_4 (and_4_out, _74112_1_p14, Hold, nTrig);
  nand nand_13 (nand_13_out, nRES, nand_12_out);
  nand nand_14 (nand_14_out, xor_1_out, xor_1_out);
  nand nand_15 (Trig, nRES, nWrEnvShape);
  // _74541 _74541_9: pin names not known; wires that end beside it: nRdNoise, nRdNoise, _74541_9_p3[0], _74541_9_p3[1], _74541_9_p3[2], _74541_9_p3[3], _74541_9_p7[0], _74541_9_p7[1], _74541_9_p7[2], _74541_9_p7[3], 1'b1, 1'b0, DA0__7[0], DA0__7[1], DA0__7[2], DA0__7[3], DA0__7[4], DA0__7[5], DA0__7[6], DA0__7[7]
  // _74273 _74273_13: pin names not known; wires that end beside it: nand_12_out, nRES, nand_14_out, _74273_13_p4, _74273_13_p5, _74273_13_p6, _74273_13_p7, _74273_13_p8, _74273_13_p9, _74273_13_p10, 1'b1, 1'b0, _74273_13_p4, _74273_13_p5, _74273_13_p6, _74273_13_p7, _74273_13_p8, _74273_13_p9, _74273_13_p10, _74273_13_p20
  // _74541 _74541_10: pin names not known; wires that end beside it: nRdEnable, nRdEnable, _74273_11_p13, _74273_11_p14, _74273_11_p15, _74273_11_p17, _74273_11_p18, 1'b0, 1'b0, 1'b0, 1'b1, 1'b0, DA0__7[0], DA0__7[1], DA0__7[2], DA0__7[3], DA0__7[4], DA0__7[5], DA0__7[6], DA0__7[7]
  not not_5 (nTrig, Trig);
  // _7474 _7474_2: pin names not known; wires that end beside it: 1'b1, _74112_1_p13, nand_1_out, 1'b1, 1'b1, and_4_out, nand_1_out, 1'b1, 1'b1, 1'b0, _74112_1_p5, _7474_2_p12
  // _7474 _7474_3: pin names not known; wires that end beside it: 1'b1, 1'b1, 1'b1, 1'b1, 1'b1, _7474_3_p6, nand_8_out, 1'b1, 1'b1, 1'b0, _7474_3_p11, _7474_3_p6
  // _74541 _74541_11: pin names not known; wires that end beside it: nRdEnvShape, nRdEnvShape, _74273_12_p13, _74273_12_p14, Attack, _74273_12_p16, 1'b0, 1'b0, 1'b0, 1'b0, 1'b1, 1'b0, DA0__7[0], DA0__7[1], DA0__7[2], DA0__7[3], DA0__7[4], DA0__7[5], DA0__7[6], DA0__7[7]
  // _74273 _74273_14: pin names not known; wires that end beside it: nand_12_out, nRES, _74273_13_p20, _74273_14_p4, _74273_14_p5, _74273_14_p6, _74273_14_p7, _74273_14_p8, _74273_14_p9, _74273_14_p10, 1'b1, 1'b0, _74273_14_p4, _74273_14_p5, _74273_14_p6, _74273_14_p7, _74273_14_p8, _74273_14_p10, _74273_14_p19
  and and_5 (and_5_out, _74273_12_p14, _74273_12_p16);
  and and_6 (and_6_out, _74112_1_p13, nHold, Alt);
  and and_7 (and_7_out, _7474_2_p12, Alt);
  and and_8 (and_8_out, nAlt, and_4_out);
  // _744040 _744040_7: pin names not known; wires that end beside it: CLK_16, nand_13_out
  not not_6 (not_6_out, _74273_12_p16);
  and and_9 (and_9_out, Attack, not_6_out);
  or or_3 (or_3_out, and_6_out, nand_1_out);
  or or_4 (or_4_out, and_7_out, and_8_out);
  // _74273 _74273_15: pin names not known; wires that end beside it: nand_12_out, nRES, _74273_14_p19, _74273_15_p4, 1'b0, 1'b0, 1'b0, 1'b0, 1'b0, 1'b0, 1'b1, 1'b0
  or or_5 (Hold, _74273_12_p13, not_6_out);
  or or_6 (Alt, and_5_out, and_9_out);
  or or_7 (or_7_out, or_3_out, or_4_out);
  not not_7 (nHold, Hold);
  not not_8 (nAttack, Attack);
  not not_9 (nAlt, Alt);
  // _7485 _7485_14: pin names not known; wires that end beside it: 1'b0, 1'b1, 1'b0, 1'b1, 1'b0, _7485_14_p6, _7485_14_p7, _7485_14_p8
  // _7485 _7485_15: pin names not known; wires that end beside it: _7485_14_p6, _7485_14_p7, _7485_14_p8, 1'b1, 1'b0, _7485_15_p6
  or or_8 (or_8_out, _74273_11_p13, _7474_1_p11);
  or or_9 (or_9_out, _74273_11_p16, _74273_15_p4);
  or or_10 (or_10_out, _74273_11_p14, _7474_1_p13);
  or or_11 (or_11_out, _74273_11_p17, _74273_15_p4);
  or or_12 (or_12_out, _74273_11_p15, _7474_3_p11);
  or or_13 (or_13_out, _74273_11_p18, _74273_15_p4);
  // _74191 _74191_1: pin names not known; wires that end beside it: nAttack, nTrig, _74112_2_p13, or_7_out, 1'b0, nAttack, nAttack, nAttack, 1'b1, 1'b0, _74191_1_p11[0], _74191_1_p11[1], _74191_1_p11[2], _74191_1_p11[3], _74191_1_p15
  not not_10 (_74112_1_p4, _74191_1_p15);
  nand nand_16 (nand_16_out, or_8_out, or_9_out);
  nand nand_17 (nand_17_out, or_10_out, or_11_out);
  nand nand_18 (nand_18_out, or_12_out, or_13_out);
  // _74273 _74273_16: pin names not known; wires that end beside it: nWrAmplitudeB, nRES, DA0__7[0], DA0__7[1], DA0__7[2], DA0__7[3], DA0__7[4], 1'b0, 1'b0, 1'b0, 1'b1, 1'b0, _74273_16_p13, _74273_16_p14, _74273_16_p15, _74273_16_p16, _74273_16_p17
  // _74273 _74273_17: pin names not known; wires that end beside it: nWrAmplitudeC, nRES, DA0__7[0], DA0__7[1], DA0__7[2], DA0__7[3], DA0__7[4], 1'b0, 1'b0, 1'b0, 1'b1, 1'b0, _74273_17_p13, _74273_17_p14, _74273_17_p15, _74273_17_p16, _74273_17_p17
  // _74273 _74273_18: pin names not known; wires that end beside it: nWrAmplitudeA, nRES, DA0__7[0], DA0__7[1], DA0__7[2], DA0__7[3], DA0__7[4], 1'b0, 1'b0, 1'b0, 1'b1, 1'b0, _74273_18_p13, _74273_18_p14, _74273_18_p15, _74273_18_p16, _74273_18_p17
  // _74541 _74541_12: pin names not known; wires that end beside it: nRdAmplitudeC, nRdAmplitudeC, _74273_17_p13, _74273_17_p14, _74273_17_p15, _74273_17_p16, _74273_17_p17, 1'b0, 1'b0, 1'b0, 1'b1, 1'b0, DA0__7[0], DA0__7[1], DA0__7[2], DA0__7[3], DA0__7[4], DA0__7[5], DA0__7[6], DA0__7[7]
  // _74541 _74541_13: pin names not known; wires that end beside it: nRdAmplitudeA, nRdAmplitudeA, _74273_18_p13, _74273_18_p14, _74273_18_p15, _74273_18_p16, _74273_18_p17, 1'b0, 1'b0, 1'b0, 1'b1, 1'b0, DA0__7[0], DA0__7[1], DA0__7[2], DA0__7[3], DA0__7[4], DA0__7[5], DA0__7[6], DA0__7[7]
  // _74541 _74541_14: pin names not known; wires that end beside it: nRdAmplitudeB, nRdAmplitudeB, _74273_16_p13, _74273_16_p14, _74273_16_p15, _74273_16_p16, _74273_16_p17, 1'b0, 1'b0, 1'b0, 1'b1, 1'b0, DA0__7[0], DA0__7[1], DA0__7[2], DA0__7[3], DA0__7[4], DA0__7[5], DA0__7[6], DA0__7[7]
  // _74157 _74157_1: pin names not known; wires that end beside it: _74273_18_p17, _74273_18_p13, _74273_18_p14, _74273_18_p15, _74273_18_p16, _74191_1_p11[0], _74191_1_p11[1], _74191_1_p11[2], _74191_1_p11[3], 1'b0, 1'b1, 1'b0, _74157_1_p16[0], _74157_1_p16[1], _74157_1_p16[2], _74157_1_p16[3]
  // _74157 _74157_2: pin names not known; wires that end beside it: _74273_16_p17, _74273_16_p13, _74273_16_p14, _74273_16_p15, _74273_16_p16, _74191_1_p11[0], _74191_1_p11[1], _74191_1_p11[2], _74191_1_p11[3], 1'b0, 1'b1, 1'b0, _74157_2_p16[0], _74157_2_p16[1], _74157_2_p16[2], _74157_2_p16[3]
  // _74157 _74157_3: pin names not known; wires that end beside it: _74273_17_p17, _74273_17_p13, _74273_17_p14, _74273_17_p15, _74273_17_p16, _74191_1_p11[0], _74191_1_p11[1], _74191_1_p11[2], _74191_1_p11[3], 1'b0, 1'b1, 1'b0, _74157_3_p13[0], _74157_3_p13[1], _74157_3_p13[2], _74157_3_p13[3]
  // _74138 _74138_5: pin names not known; wires that end beside it: _74157_1_p16[0], _74157_1_p16[2], _74157_1_p16[1], 1'b1, nand_16_out, _74157_1_p16[3], 1'b1, 1'b0, _74138_5_p9, _74138_5_p10, _74138_5_p11, _74138_5_p12, _74138_5_p13, _74138_5_p14, _74138_5_p15, _74138_5_p16
  // _74138 _74138_6: pin names not known; wires that end beside it: _74157_1_p16[0], _74157_1_p16[2], _74157_1_p16[1], _74157_1_p16[3], nand_16_out, 1'b0, 1'b1, 1'b0, _74138_6_p9, _74138_6_p10, _74138_6_p11, _74138_6_p12, _74138_6_p13, _74138_6_p14, _74138_6_p15, _74138_6_p16
  // _74138 _74138_7: pin names not known; wires that end beside it: _74157_2_p16[0], _74157_2_p16[2], _74157_2_p16[1], 1'b1, nand_17_out, _74157_2_p16[3], 1'b1, 1'b0, _74138_7_p9, _74138_7_p10, _74138_7_p11, _74138_7_p12, _74138_7_p13, _74138_7_p14, _74138_7_p15, _74138_7_p16
  // _74138 _74138_8: pin names not known; wires that end beside it: _74157_2_p16[0], _74157_2_p16[2], _74157_2_p16[1], _74157_2_p16[3], nand_17_out, 1'b0, 1'b1, 1'b0, _74138_8_p9, _74138_8_p10, _74138_8_p11, _74138_8_p12, _74138_8_p13, _74138_8_p14, _74138_8_p15, _74138_8_p16
  // _74138 _74138_9: pin names not known; wires that end beside it: _74157_3_p13[0], _74157_3_p13[2], _74157_3_p13[1], 1'b1, nand_18_out, _74157_3_p13[3], 1'b1, 1'b0, _74138_9_p9, _74138_9_p10, _74138_9_p11, _74138_9_p12, _74138_9_p13, _74138_9_p14, _74138_9_p15, _74138_9_p16
  // _74138 _74138_10: pin names not known; wires that end beside it: _74157_3_p13[0], _74157_3_p13[2], _74157_3_p13[1], _74157_3_p13[3], nand_18_out, 1'b0, 1'b1, 1'b0, _74138_10_p9, _74138_10_p10, _74138_10_p11, _74138_10_p12, _74138_10_p13, _74138_10_p14, _74138_10_p15, _74138_10_p16
  // _74125 _74125_1: pin names not known; wires that end beside it: 1'b1, 1'b1, 1'b1, 1'b1, _74138_5_p9, _74138_5_p10, _74138_5_p11, _74138_5_p12, 1'b1, 1'b0, _74125_1_p11, _74125_1_p12, _74125_1_p13, _74125_1_p14, AnalogChA
  // _74125 _74125_2: pin names not known; wires that end beside it: 1'b1, 1'b1, 1'b1, 1'b1, _74138_5_p13, _74138_5_p14, _74138_5_p15, _74138_5_p16, 1'b1, 1'b0, _74125_2_p11, _74125_2_p12, _74125_2_p13, _74125_2_p14
  // _74125 _74125_3: pin names not known; wires that end beside it: 1'b1, 1'b1, 1'b1, 1'b1, _74138_6_p9, _74138_6_p10, _74138_6_p11, _74138_6_p12, 1'b1, 1'b0, _74125_3_p11, _74125_3_p12, _74125_3_p13, _74125_3_p14
  // _74125 _74125_4: pin names not known; wires that end beside it: 1'b1, 1'b1, 1'b1, 1'b1, _74138_6_p13, _74138_6_p14, _74138_6_p15, _74138_6_p16, 1'b1, 1'b0, _74125_4_p11, _74125_4_p12, _74125_4_p13, _74125_4_p14
  // _74125 _74125_5: pin names not known; wires that end beside it: 1'b1, 1'b1, 1'b1, 1'b1, _74138_7_p9, _74138_7_p10, _74138_7_p11, _74138_7_p12, 1'b1, 1'b0, _74125_5_p11, _74125_5_p12, _74125_5_p13, _74125_5_p14, AnalogChB
  // _74125 _74125_6: pin names not known; wires that end beside it: 1'b1, 1'b1, 1'b1, 1'b1, _74138_7_p13, _74138_7_p14, _74138_7_p15, _74138_7_p16, 1'b1, 1'b0, _74125_6_p11, _74125_6_p12, _74125_6_p13, _74125_6_p14
  // _74125 _74125_7: pin names not known; wires that end beside it: 1'b1, 1'b1, 1'b1, 1'b1, _74138_8_p9, _74138_8_p10, _74138_8_p11, _74138_8_p12, 1'b1, 1'b0, _74125_7_p11, _74125_7_p12, _74125_7_p13, _74125_7_p14
  // _74125 _74125_8: pin names not known; wires that end beside it: 1'b1, 1'b1, 1'b1, 1'b1, _74138_8_p13, _74138_8_p14, _74138_8_p15, _74138_8_p16, 1'b1, 1'b0, _74125_8_p11, _74125_8_p12, _74125_8_p13, _74125_8_p14
  // _74125 _74125_9: pin names not known; wires that end beside it: 1'b1, 1'b1, 1'b1, 1'b1, _74138_9_p9, _74138_9_p10, _74138_9_p11, _74138_9_p12, 1'b1, 1'b0, _74125_9_p11, _74125_9_p12, _74125_9_p13, _74125_9_p14, AnalogChC
  // _74125 _74125_10: pin names not known; wires that end beside it: 1'b1, 1'b1, 1'b1, 1'b1, _74138_9_p13, _74138_9_p14, _74138_9_p15, _74138_9_p16, 1'b1, 1'b0, _74125_10_p11, _74125_10_p12, _74125_10_p13, _74125_10_p14
  // _74125 _74125_11: pin names not known; wires that end beside it: 1'b1, 1'b1, 1'b1, 1'b1, _74138_10_p9, _74138_10_p10, _74138_10_p11, _74138_10_p12, 1'b1, 1'b0, _74125_11_p11, _74125_11_p12, _74125_11_p13, _74125_11_p14
  // _74125 _74125_12: pin names not known; wires that end beside it: 1'b1, 1'b1, 1'b1, 1'b1, _74138_10_p13, _74138_10_p14, _74138_10_p15, _74138_10_p16, 1'b1, 1'b0, _74125_12_p11, _74125_12_p12, _74125_12_p13, _74125_12_p14
  PullDown pulldown_1 (.out(_74125_1_p11));
  PullDown pulldown_2 (.out(_74125_1_p12));
  PullDown pulldown_3 (.out(_74125_1_p13));
  PullDown pulldown_4 (.out(_74125_1_p14));
  PullDown pulldown_5 (.out(_74125_2_p11));
  PullDown pulldown_6 (.out(_74125_2_p12));
  PullDown pulldown_7 (.out(_74125_2_p13));
  PullDown pulldown_8 (.out(_74125_2_p14));
  PullDown pulldown_9 (.out(_74125_3_p11));
  PullDown pulldown_10 (.out(_74125_3_p12));
  PullDown pulldown_11 (.out(_74125_3_p13));
  PullDown pulldown_12 (.out(_74125_3_p14));
  PullDown pulldown_13 (.out(_74125_4_p11));
  PullDown pulldown_14 (.out(_74125_4_p12));
  PullDown pulldown_15 (.out(_74125_4_p13));
  PullDown pulldown_16 (.out(_74125_4_p14));
  PullDown pulldown_17 (.out(AnalogChA));
  PullDown pulldown_18 (.out(_74125_5_p11));
  PullDown pulldown_19 (.out(_74125_5_p12));
  PullDown pulldown_20 (.out(_74125_5_p13));
  PullDown pulldown_21 (.out(_74125_5_p14));
  PullDown pulldown_22 (.out(_74125_6_p11));
  PullDown pulldown_23 (.out(_74125_6_p12));
  PullDown pulldown_24 (.out(_74125_6_p13));
  PullDown pulldown_25 (.out(_74125_6_p14));
  PullDown pulldown_26 (.out(_74125_7_p11));
  PullDown pulldown_27 (.out(_74125_7_p12));
  PullDown pulldown_28 (.out(_74125_7_p13));
  PullDown pulldown_29 (.out(_74125_7_p14));
  PullDown pulldown_30 (.out(_74125_8_p11));
  PullDown pulldown_31 (.out(_74125_8_p12));
  PullDown pulldown_32 (.out(_74125_8_p13));
  PullDown pulldown_33 (.out(_74125_8_p14));
  PullDown pulldown_34 (.out(AnalogChB));
  PullDown pulldown_35 (.out(_74125_9_p11));
  PullDown pulldown_36 (.out(_74125_9_p12));
  PullDown pulldown_37 (.out(_74125_9_p13));
  PullDown pulldown_38 (.out(_74125_9_p14));
  PullDown pulldown_39 (.out(_74125_10_p11));
  PullDown pulldown_40 (.out(_74125_10_p12));
  PullDown pulldown_41 (.out(_74125_10_p13));
  PullDown pulldown_42 (.out(_74125_10_p14));
  PullDown pulldown_43 (.out(_74125_11_p11));
  PullDown pulldown_44 (.out(_74125_11_p12));
  PullDown pulldown_45 (.out(_74125_11_p13));
  PullDown pulldown_46 (.out(_74125_11_p14));
  PullDown pulldown_47 (.out(_74125_12_p11));
  PullDown pulldown_48 (.out(_74125_12_p12));
  PullDown pulldown_49 (.out(_74125_12_p13));
  PullDown pulldown_50 (.out(_74125_12_p14));
  PullDown pulldown_51 (.out(AnalogChC));

  // Notes on the sheet:
  //   nRESET: default 1
  //   ENVELOPE RATE
  //   BC1/BDIR
  //   =========
  //   0 /0 = Idle
  //   1 / 0 = Read Data
  //   0 / 1 = Write Data
  //   1 /1 = Address
  //   -------------------------------
  //   Implementation of AY-3-8910 using
  //   discrete 74-series logic ICs.
  //   (c) 2022 Mats Engstrom 
  //   mats.engstrom@protonmail.ch
  //   Project fiiles available at
  //   github.com/mengstr/Discrete-AY-3-8910
  //   Released under the MIT license
  //   -------------------------------
  //   CONTROL & CLK GEN
  //   TONE GENERATOR A
  //   TONE GENERATOR B
  //   TONE GENERATOR C
  //   NOISE GENERATOR
  //   ENVELOPE
  //   ENABLE/MIXER
  //   Hold
  //   Alternate
  //   Attack
  //   Continue
  //   AT AL HO
  //   -------------------
  //   0 . 0 .  0   Falling sawtooth
  //   0 . 0 . 1   Fall & stop
  //   0 . 1 . 0   Falling triangle
  //   0 . 1 . 1   Fall & Jump top
  //   1 . 0 . 0   Rising Sawtooth
  //   1 . 0 . 1   Rise & stop
  //   1 . 1 . 0   Rising triangle
  //   1 . 1 . 1   Rise & Jump zero
  //   If Continue==0
  //   0xx -> 001
  //   1xx -> 111
  //   AMPLITUDE CONTROL A
  //   AMPLITUDE CONTROL B
  //   AMPLITUDE CONTROL C
  //   D/A CONVERTER A
  //   D/A CONVERTER B
  //   D/A CONVERTER C
endmodule
